# Fritzing sketch circuit-layout (saved by Fritzing 1.0.2b)
breadboards: 1

parts:
  MCU1 = Raspberry Pi Zero
  Q1 = NPN-Transistor [package="TO92 [THT]"]
  LED1 = LED - 5mm [color="Infrared (940nm)" current=0.030A package="5 mm [THT]"]
  R1 = Resistor [tolerance=±5% power=0.25W resistance=220 package=THT]

nets:
  N1: MCU1.pin_2, MCU1.pin_4, LED1.anode
  N2: MCU1.pin_10, R1.Pin_1
  N3: MCU1.pin_14, MCU1.pin_30, Q1.E
  N4: Q1.B, R1.Pin_0
  N5: Q1.C, LED1.cathode

notes:
  BCN-337 transistor
  220 Ohm resistor
